# Fritzing sketch master (saved by Fritzing 0.9.5d)
circuit board: 8.46667cm x 5.64444cm

parts:
  M1 = DOIT Esp32 DevKit v1 (30 pins long, 11 pins width) [part_number=ESP32S-PIN30]
  M2 = Pzem-004t
  M3 = Pzem-004t
  M4 = Pzem-004t
  Mod1 = KY-022 Infrared Receiver Module [package="Breakout board"]
  S1 = SWITCH-MOMENTARY-2 [package=tactile-pth-12mm]
  S2 = SWITCH-MOMENTARY-2 [package=tactile-pth-12mm]
  S3 = SWITCH-MOMENTARY-2 [package=tactile-pth-12mm]
  LCD2004-I2C1 = LCD2004-I2C
  JACK1 = 2.1mm Barrel Jack with Terminal Block
  M5 = RioRand LM2596
  R1 = RPACK* [package=rpack-sip-pth-5]
  R2 = Resistor [tolerance=±5% resistance=220 package="2010 [SMD]"]
  R3 = Resistor [tolerance=±5% resistance=220 package="2010 [SMD]"]
  R4 = Resistor [tolerance=±5% resistance=220 package="2010 [SMD]"]
  R5 = RPACK* [package=rpack-sip-pth-5]
  R6 = RPACK* [package=rpack-sip-pth-5]
  R7 = RPACK* [package=rpack-sip-pth-5]
  microSD1 = MicroSD Card Module
  RTC1 = DS3231 AT24C32 Real Time Clock

nets:
  VCC: M1.3V3, R7.1, microSD1.VCC, RTC1.VCC
  GND: M1.GND, LCD2004-I2C1.GND, M5.Pin_4, R1.1, R5.1, microSD1.GND
  N1: M1.D4, Mod1.S
  N2: M1.RX2, M2.TX, M3.TX, M4.TX
  N3: M1.TX2, M2.RX, M3.RX, M4.RX
  N4: M1.D5, microSD1.CS
  N5: M1.D18, microSD1.SCK
  N6: M1.D19, microSD1.MISO
  N7: M1.D21, LCD2004-I2C1.SDA, RTC1.SDA
  N8: M1.D22, LCD2004-I2C1.SCL, RTC1.SCL
  N9: M1.D23, microSD1.MOSI
  N10: M1.D34, S3.2, R2.Pin_0
  N11: M1.D35, S2.2, R3.Pin_0
  N12: M1.D32, S1.2, R4.Pin_0
  VIN: M1.VIN, LCD2004-I2C1.VCC, M5.Pin_3, R6.1
  N13: M2.5V, R6.4
  N14: M2.GND, R5.4
  N15: M3.5V, R6.5
  N16: M3.GND, R5.5
  N17: M4.5V, R6.6
  N18: M4.GND, R5.6
  N19: Mod1.-, R5.3
  N20: Mod1.Vin, R6.2
  N21: S1.1, R1.4
  N22: S2.1, R1.5
  N23: S3.1, R1.6
  N24: JACK1.POS, M5.Pin_2
  N25: JACK1.NEG, M5.Pin_1
  N26: R1.3, RTC1.GND
  N27: R2.Pin_1, R7.6
  N28: R3.Pin_1, R7.5
  N29: R4.Pin_1, R7.4

custom parts:
  DOIT Esp32 DevKit v1 (30 pins long, 11 pins width): The DOIT Esp32 DevKit v1 is one of the development board created by DOIT to evaluate the ESP-WROOM-32 module. It is based on the ESP32 microcontroller that boasts Wifi, Bluetooth, Ethernet and Low Power support all in a single chip. (vanepp) made breadboard work, adjusted pin numbering and labels and reduced size of schematic and cleaned up pcb. This chip is 30pins long (2 x15) and 11 pins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
  Pzem-004t: Pzem-004t used for measuring AC voltage, current, active power, frequency, power factor and active energy, the module is without display function, the data is read through the TTL interface.
  KY-022 Infrared Receiver Module: KY-022 IR receiver module, reacts to 38kHz infrared light.
  LCD2004-I2C: A standard character display with 4x20 characters. Comes in many colors with LCM2004 IIC attached.
  MicroSD Card Module: A common microSD card module.
  DS3231 AT24C32 Real Time Clock: Real-time clock basedo on chip DS3231, plus memory chip AT24C32 (32 Kb storage capacity). On-chip temperature sensor with an accuracy of ±3 ℃, I2C bus interface maximum speed: 400 kHz. Operating voltage: 3.3 V to 5.5 V with battery backup capabilities.
