# Fritzing sketch slave (saved by Fritzing 0.9.5d)

parts:
  M1 = DOIT Esp32 DevKit v1 (30 pins long, 11 pins width) [part_number=ESP32S-PIN30]
  LED1 = LED - 5mm [color="Green (570nm)" package="5 mm [THT]"]
  LED2 = LED - 5mm [color="Red (633nm)" package="5 mm [THT]"]
  IR2 = tl1838 [package=THT]
  U1 = RFID RC522 SIP - 8 pins [chip_label="RFID RC522" package="SIP (Single Inline) [THT]"]
  M2 = fc-51 [package=THT]
  JACK1 = 2.1mm Barrel Jack with Terminal Block
  M3 = RioRand LM2596
  R1 = Resistor [tolerance=±5% resistance=220 package="0402 [SMD]"]
  R2 = Resistor [tolerance=±5% resistance=220 package="0402 [SMD]"]
  A1 = DHT22 module
  J1 = Piezo Speaker

nets:
  VCC: M1.3V3, IR2.VCC, U1.VCC, M2.pin3, R1.Pin_1, R2.Pin_1, A1.VCC
  GND: M1.GND, LED1.cathode, LED2.cathode, IR2.GND, U1.GND, M2.pin2, M3.Pin_4, A1.GND, J1.pin1
  N1: M1.D15, A1.DAT
  N2: M1.D4, IR2.OUT
  N3: M1.D5, U1.NSS
  N4: M1.D18, U1.SCK
  N5: M1.D19, U1.MISO
  N6: M1.D22, U1.RST
  N7: M1.D23, U1.MOSI
  N8: M1.D27, J1.pin2
  N9: M1.D13, M2.pin1
  N10: M1.VIN, M3.Pin_3
  N11: LED1.anode, R1.Pin_0
  N12: LED2.anode, R2.Pin_0
  N13: JACK1.POS, M3.Pin_2
  N14: JACK1.NEG, M3.Pin_1

custom parts:
  DOIT Esp32 DevKit v1 (30 pins long, 11 pins width): The DOIT Esp32 DevKit v1 is one of the development board created by DOIT to evaluate the ESP-WROOM-32 module. It is based on the ESP32 microcontroller that boasts Wifi, Bluetooth, Ethernet and Low Power support all in a single chip. (vanepp) made breadboard work, adjusted pin numbering and labels and reduced size of schematic and cleaned up pcb. This chip is 30pins long (2 x15) and 11 pins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
  tl1838: The TL1838 is a miniaturized receiver for infrared remote control systems. A PIN diode and a preamplifier are assembled on a lead frame, the epoxy package acts as an IR filter. The demodulated output signal can be directly decoded by a microprocessor.
  RFID RC522 SIP - 8 pins: A SIP stand-in part for RFID RC522 . With 8 pins on a 300 mil single inline package (SIP) footprint.
  DHT22 module: DHT22 module. Pins GND VCC Data.
